// Logisim project TinyCPU-AddressPath.circ as structural Verilog: 1 circuit, main circuit AddressPath
module AddressPath (
  input  [11:0] ADDRESS_IN,
  input  AR_LOAD,
  input  [11:0] OFFSET,
  input  VALID_IN,
  input  CLK,
  output [11:0] ADDRESS,
  output [11:0] ADDRESS_PLUS_OFFSET,
  output OFFSET_CARRY,
  output ADDRESS_VALID
);

  wire undriven;
  wire [11:0] AR_q;

  Register #(.width(12)) AR (.D(ADDRESS_IN), .en(AR_LOAD), .clk(CLK), .Q(AR_q));  // open: clr
  Register #(.width(1)) AR_VALID (.D(VALID_IN), .en(undriven), .clk(CLK), .Q(ADDRESS_VALID));  // open: clr
  Adder #(.width(12)) OFFSET_ADDER (.out(ADDRESS_PLUS_OFFSET), .cout(OFFSET_CARRY));  // open: a, b, cin

  // Notes on the sheet:
  //   Clocked 12-bit address register with combinational offset addition
endmodule
