// Logisim project TinyCPU-FetchDecode.circ as structural Verilog: 1 circuit, main circuit FetchDecode
module FetchDecode (
  input  CLK,
  input  RESET,
  input  ZERO,
  input  [11:0] PROGRAM_LIMIT,
  input  NEGATIVE,
  input  ERROR,
  output [15:0] OPERAND,
  output LOAD_CONST,
  output STORE_ADDRESS,
  output ADD_ADDRESS,
  output JUMP_NOT_ZERO,
  output PRINT,
  output HALT,
  output SET_ADDR,
  output HALT_ERROR,
  output [11:0] PC_OUT,
  output LOAD_ADDRESS,
  output LOAD_ADDRESS_REGISTER,
  output LOAD_ADDRESS_REGISTER_PLUS_OFFSET,
  output ADD_CONST,
  output ADD_ADDRESS_REGISTER,
  output ADD_ADDRESS_REGISTER_PLUS_OFFSET,
  output SUB_CONST,
  output SUB_ADDRESS,
  output SUB_ADDRESS_REGISTER,
  output SUB_ADDRESS_REGISTER_PLUS_OFFSET,
  output MUL_CONST,
  output MUL_ADDRESS,
  output MUL_ADDRESS_REGISTER,
  output MUL_ADDRESS_REGISTER_PLUS_OFFSET,
  output DIV_CONST,
  output DIV_ADDRESS,
  output DIV_ADDRESS_REGISTER,
  output DIV_ADDRESS_REGISTER_PLUS_OFFSET,
  output AND_CONST,
  output AND_ADDRESS,
  output AND_ADDRESS_REGISTER,
  output AND_ADDRESS_REGISTER_PLUS_OFFSET,
  output OR_CONST,
  output OR_ADDRESS,
  output OR_ADDRESS_REGISTER,
  output OR_ADDRESS_REGISTER_PLUS_OFFSET,
  output STORE_ADDRESS_REGISTER,
  output STORE_ADDRESS_REGISTER_PLUS_OFFSET,
  output LOAD_ADDRESS_REGISTER_CONST,
  output LOAD_ADDRESS_REGISTER_ADDRESS,
  output NOT,
  output JUMP_ADDRESS,
  output JUMP_ZERO,
  output JUMP_NEGATIVE,
  output JUMP_ERROR,
  output JUMP_NOT_ERROR,
  output CLEAR_ERROR,
  output INPUT,
  output PRINT_ADDRESS,
  output SET_OVF,
  output SET_DIV0,
  output SET_INV,
  output SET_ILL,
  output SET_INPUT
);

  wire [5:0] undriven_2;
  wire [15:12] undriven;

  Register #(.width(16)) PC ();  // open: D, en, clk, Q, clr
  Adder #(.width(12)) PC_INCREMENT (
    .a({PROGRAM_LIMIT[11:1], CLK}), .out({PROGRAM_LIMIT[11:1], CLK}), .cin(CLK), .cout(CLK));  // open: b
  Multiplexer #(.width(12)) PC_SOURCE (.out({PROGRAM_LIMIT[11:1], CLK}));  // open: in0, in1, sel
  ROM #(.addrWidth(12), .dataWidth(22)) INSTRUCTION_ROM ();  // open: addr, data
  Comparator #(.width(12)) PC_RANGE (
    .a({PROGRAM_LIMIT[11:1], CLK}), .b({PROGRAM_LIMIT[11:1], CLK}), .gt(CLK), .eq(CLK));  // open: lt
  Decoder #(.select(6)) ISA_DECODER (
    .out63(OPERAND[0]), .sel(undriven_2), .en(undriven_2[0]));  // open: out0, out1, out2, out3, out4, out5, out6, out7, out8, out9, out10, out11, out12, out13, out14, out15, out16, out17, out18, out19, out20, out21, out22, out23, out24, out25, out26, out27, out28, out29, out30, out31, out32, out33, out34, out35, out36, out37, out38, out39, out40, out41, out42, out43, out44, out45, out46, out47, out48, out49, out50, out51, out52, out53, out54, out55, out56, out57, out58, out59, out60, out61, out62
  // AND_Gate JNZ_TAKEN has open pins: out=CLK
  // OR_Gate ERROR_HALT has open pins: out=CLK
  // Pins of 1 and 12 and 22 bits meet at {OPERAND[5:0], undriven, PROGRAM_LIMIT[11:1], CLK}
  // Pins of 1 and 6 and 16 bits meet at OPERAND
  // Pins of 1 and 6 bits meet at undriven_2

  assign ERROR = CLK;
  assign HALT_ERROR = CLK;
  assign NEGATIVE = CLK;
  assign PC_OUT = {PROGRAM_LIMIT[11:1], CLK};
  assign PROGRAM_LIMIT[0] = CLK;
  assign RESET = CLK;
  assign SET_ADDR = CLK;

  // Notes on the sheet:
  //   AP 7 machine format v1: stable six-bit opcode allocation and encoder-generated ROM
  //   contents of INSTRUCTION_ROM (hex, n*v repeats v):
  //   00ffff 1c0065 000003 1c0064 2a0000 050065 1c0064 240004 2c0000
endmodule
