// Logisim project TinyCPU-Memory.circ as structural Verilog: 1 circuit, main circuit Memory
module Memory (
  input  [11:0] ADDRESS,
  input  WRITE_ENABLE,
  input  CLK,
  input  VALID_IN,
  input  [15:0] DATA_IN,
  output VALID_OUT,
  output [15:0] DATA_OUT
);

  RAM #(.addrWidth(12), .dataWidth(1)) VALID_RAM (
    .addr(ADDRESS), .we(WRITE_ENABLE), .clk(CLK), .din(VALID_IN), .dout(VALID_OUT));  // open: oe
  RAM #(.addrWidth(12), .dataWidth(16)) DATA_RAM (
    .addr(ADDRESS), .we(WRITE_ENABLE), .clk(CLK), .din(DATA_IN), .dout(DATA_OUT));  // open: oe

  // Notes on the sheet:
  //   4096-word value/valid memory with shared address, write-enable, and clock
endmodule
